// Logisim project problem2.circ as structural Verilog
module main (
  input  in_1,
  input  in_2,
  input  in_3,
  input  in_4,
  input  in_5,
  input  in_6,
  input  in_7,
  input  in_8,
  input  in_9,
  input  in_10,
  input  in_11,
  output out_12
);

  problem2 problem2_1 (
    .d0(in_1), .d1(in_2), .d2(in_3), .d3(in_4), .d4(in_5), .d5(in_6), .d6(in_7), .d7(in_8), .s2(in_9),
    .s1(in_10), .s0(in_11), .y(out_12));
endmodule

// VHDL entity problem2, as the project stores it:
library ieee;
use ieee.std_logic_1164.all;

entity problem2 is
    port (
        d0, d1, d2, d3 : in std_logic;
        d4, d5, d6, d7 : in std_logic;
        s2, s1, s0     : in std_logic;
        y              : out std_logic
    );
end problem2;

architecture behavioral of problem2 is
    signal sel : std_logic_vector(2 downto 0);
begin
    sel <= s2 & s1 & s0;

    with sel select
        y <= d0 when "000",
             d1 when "001",
             d2 when "010",
             d3 when "011",
             d4 when "100",
             d5 when "101",
             d6 when "110",
             d7 when "111",
             '0' when others;
end behavioral;
